// Logisim project Clk.circ as structural Verilog: 9 circuits, main circuit CLK
module CLK (
  input  A_M,
  input  MCLK,
  input  HLT,
  output CLK
);

  wire and_1_out, and_2_out, clock_1_out, j_k_ff_1_q, j_k_ff_1_qn, not_1_out, or_1_out;

  Clock clock_1 (.out(clock_1_out));
  J_K_Flip_Flop j_k_ff_1 (
    .J(A_M), .clk(A_M), .K(A_M), .Q(j_k_ff_1_q), .Qn(j_k_ff_1_qn), .en(A_M));  // open: preset, reset
  not not_1 (not_1_out, HLT);
  and and_1 (and_1_out, clock_1_out, j_k_ff_1_q);
  and and_2 (and_2_out, j_k_ff_1_qn, MCLK);
  or or_1 (or_1_out, and_1_out, and_2_out);
  and and_3 (CLK, or_1_out, not_1_out);
  // also tied to GND on the sheet: HLT
endmodule

module A_Reg (
  input  in_1,
  input  [7:0] in_2,
  input  in_3,
  input  in_4,
  output [7:0] out_5,
  output [7:0] out_6
);

  Register register_1 (.D(in_2), .en(in_3), .Q(out_5), .clk(in_1));  // open: clr
  assign out_6 = in_4 ? out_5 : 8'bz;  // Controlled_Buffer controlled_buffer_1
endmodule

module B_REG (
  input  [7:0] in_1,
  input  in_2,
  input  in_3,
  output [7:0] out_4
);

  Register register_1 (.D(in_1), .en(in_2), .Q(out_4), .clk(in_3));  // open: clr
endmodule

module ALU (
  input  [7:0] in_1,
  input  [7:0] in_2,
  input  in_3,
  input  in_4,
  output [7:0] out_5,
  output out_6,
  output out_7
);

  wire [7:0] adder_1_out, xor_1_out;

  Adder adder_1 (.a(in_1), .b(xor_1_out), .out(adder_1_out), .cout(out_6));  // open: cin
  assign xor_1_out = in_2 ^ {8{in_4}};  // XOR_Gate xor_1, 8 bits wide
  assign out_5 = in_3 ? adder_1_out : 8'bz;  // Controlled_Buffer controlled_buffer_1
  nor nor_1 (out_7, out_5[0], out_5[1], out_5[2], out_5[3], out_5[4], out_5[5], out_5[6], out_5[7]);
endmodule

module PC (
  input  [7:0] in_1,
  input  in_2,
  input  in_3,
  input  in_4,
  input  in_5,
  output [15:0] out_6
);

  wire and_1_out, not_1_out;
  wire [7:0] register_1_q, register_2_q;

  not not_1 (not_1_out, in_3);
  Register register_1 (.D(in_1), .en(in_3), .Q(register_1_q), .clk(in_5));  // open: clr
  Register register_2 (.D(in_1), .en(not_1_out), .Q(register_2_q), .clk(in_5));  // open: clr
  Counter #(.width(16), .max('hffff)) counter_1 (
    .load(in_2), .D({register_2_q, register_1_q}), .count(and_1_out), .Q(out_6), .clk(in_5));  // open: carry, clr
  and and_1 (and_1_out, in_4, in_5);

  // Other names for the same wires on the sheet: CLK = in_5; IN[7:0] = in_1
endmodule

module RAM (
  input  [7:0] in_1,
  input  in_2,
  input  in_3,
  input  in_4,
  input  in_5,
  input  in_6,
  output [7:0] out_7
);

  wire not_1_out;
  wire [7:0] register_1_q, register_2_q;
  wire [15:0] multiplexer_1_out, register_3_q;

  not not_1 (not_1_out, in_2);
  Register register_1 (.D(in_1), .en(in_2), .Q(register_1_q), .clk(in_3));  // open: clr
  Register register_2 (.D(in_1), .en(not_1_out), .Q(register_2_q), .clk(in_3));  // open: clr
  Register #(.width(16)) register_3 (.Q(register_3_q));  // open: D, en, clk, clr
  Multiplexer #(.width(16), .enable("false")) multiplexer_1 (
    .in0({register_2_q, register_1_q}), .in1(register_3_q), .out(multiplexer_1_out), .sel(in_6));
  RAM_part #(.addrWidth(16), .bus("separate")) ram_1 (
    .addr(multiplexer_1_out), .din(in_1), .data(out_7), .str(in_4), .clk(in_3), .ld(in_5));  // open: sel, clr

  // Other names for the same wires on the sheet: CLK = in_3; IN[7:0] = in_1
endmodule

module INST_REG (
  input  [7:0] in_1,
  input  in_2,
  input  in_3,
  output [7:0] out_4
);

  Register register_1 (.D(in_1), .en(in_2), .Q(out_4), .clk(in_3));  // open: clr
endmodule

module CONTROL (
  input  [7:0] in_1,
  input  in_2,
  input  in_3,
  output out_4,
  output out_5,
  output out_6,
  output out_7,
  output out_8,
  output out_9,
  output out_10,
  output out_11,
  output out_12,
  output out_13,
  output out_14,
  output out_15,
  output out_16,
  output out_17
);

  ROM #(.addrWidth(10), .dataWidth(14)) rom_1 (
    .addr({in_3, in_2, in_1}),
    .data({out_17, out_16, out_15, out_14, out_13, out_12, out_11, out_10, out_9, out_8, out_7, out_6, out_5, out_4}));  // open: sel

  // Notes on the sheet:
  //   contents of rom_1 (hex, n*v repeats v):
  //   16*0 1 1006*0 1111
endmodule

module CPU (
);

  wire AI, AL, alu_1_out_7, ALUSUB, ALUW, BI, button_1_out, button_2_out, CF, CLK, HLT, INSTEN, PCLE, PCLRS,
       PCOUNT, RAMAINS, RAMBLOAD, RAMLRS, RAMWM, ZF;
  wire [7:0] _8BUS, a_reg_1_out_5, b_reg_1_out_4, inst_reg_1_out_4;
  wire [15:0] _16BUS;

  Button button_1 (.out(button_1_out));
  Button button_2 (.out(button_2_out));
  CLK clk_1 (.HLT(HLT), .CLK(CLK), .A_M(button_1_out), .MCLK(button_2_out));
  PC pc_1 (.in_1(_8BUS), .in_2(PCLE), .in_3(PCLRS), .in_4(PCOUNT), .in_5(CLK), .out_6(_16BUS));
  RAM ram_1 (.in_1(_8BUS), .in_2(RAMLRS), .in_3(CLK), .out_7(_8BUS), .in_6(RAMAINS), .in_4(RAMWM), .in_5(RAMBLOAD));
  INST_REG inst_reg_1 (.in_1(_8BUS), .in_2(INSTEN), .in_3(CLK), .out_4(inst_reg_1_out_4));
  A_Reg a_reg_1 (.in_1(CLK), .in_2(_8BUS), .in_3(AI), .out_5(a_reg_1_out_5), .out_6(_8BUS), .in_4(AL));
  B_REG b_reg_1 (.in_1(_8BUS), .in_2(BI), .in_3(CLK), .out_4(b_reg_1_out_4));
  CONTROL control_1 (
    .in_1(inst_reg_1_out_4), .in_2(CF), .in_3(ZF), .out_4(HLT), .out_5(AI), .out_6(AL), .out_7(BI),
    .out_8(ALUW), .out_9(ALUSUB), .out_10(PCLE), .out_11(PCLRS), .out_12(RAMLRS), .out_13(RAMAINS),
    .out_14(RAMWM), .out_15(RAMBLOAD), .out_16(INSTEN), .out_17(PCOUNT));
  Button button_3 (.out(ZF));
  ALU alu_1 (
    .in_1(a_reg_1_out_5), .in_2(b_reg_1_out_4), .in_3(ALUW), .in_4(ALUSUB), .out_5(_8BUS),
    .out_7(alu_1_out_7), .out_6(CF));
endmodule
