// Logisim project Proto.circ as structural Verilog: 9 circuits, main circuit CLK
module CLK (
  input  A_M,
  input  MCLK,
  input  HLT,
  output CLK
);

  wire and_1_out, and_2_out, clock_1_out, j_k_ff_1_q, j_k_ff_1_qn, not_1_out, or_1_out;

  Clock clock_1 (.out(clock_1_out));
  J_K_Flip_Flop j_k_ff_1 (
    .J(A_M), .clk(A_M), .K(A_M), .Q(j_k_ff_1_q), .Qn(j_k_ff_1_qn), .en(A_M));  // open: preset, reset
  not not_1 (not_1_out, HLT);
  and and_1 (and_1_out, clock_1_out, j_k_ff_1_q);
  and and_2 (and_2_out, j_k_ff_1_qn, MCLK);
  or or_1 (or_1_out, and_1_out, and_2_out);
  and and_3 (CLK, or_1_out, not_1_out);
  // also tied to GND on the sheet: HLT
endmodule

module A_Reg (
  input  in_1,
  input  [7:0] in_2,
  input  in_3,
  input  in_4,
  output [7:0] out_5,
  output [7:0] out_6
);

  Register register_1 (.D(in_2), .en(in_3), .Q(out_5), .clk(in_1));  // open: clr
  assign out_6 = in_4 ? out_5 : 8'bz;  // Controlled_Buffer controlled_buffer_1
endmodule

module B_REG (
  input  [7:0] in_1,
  input  in_2,
  input  in_3,
  output [7:0] out_4
);

  Register register_1 (.D(in_1), .en(in_2), .Q(out_4), .clk(in_3));  // open: clr
endmodule

module ALU (
  input  [7:0] in_1,
  input  [7:0] in_2,
  input  in_3,
  input  in_4,
  output [7:0] out_5,
  output out_6,
  output out_7
);

  wire [7:0] adder_1_out, xor_1_out;

  Adder adder_1 (.a(in_1), .b(xor_1_out), .out(adder_1_out), .cout(out_6));  // open: cin
  assign xor_1_out = in_2 ^ {8{in_4}};  // XOR_Gate xor_1, 8 bits wide
  assign out_5 = in_3 ? adder_1_out : 8'bz;  // Controlled_Buffer controlled_buffer_1
  nor nor_1 (out_7, adder_1_out[0], adder_1_out[1], adder_1_out[2], adder_1_out[3], adder_1_out[4], adder_1_out[5], adder_1_out[6], adder_1_out[7]);
endmodule

module PC (
  input  [7:0] in_1,
  input  in_2,
  input  in_3,
  input  in_4,
  input  in_5,
  output [15:0] out_6
);

  wire not_1_out, not_2_out;
  wire [7:0] register_1_q, register_2_q;

  not not_1 (not_1_out, in_3);
  Register register_1 (.D(in_1), .en(in_3), .Q(register_1_q), .clk(in_4));  // open: clr
  Register register_2 (.D(in_1), .en(not_1_out), .Q(register_2_q), .clk(in_4));  // open: clr
  not not_2 (not_2_out, in_5);
  Counter #(.width(16), .max('hffff)) counter_1 (
    .load(in_2), .D({register_2_q, register_1_q}), .count(not_2_out), .Q(out_6), .clk(in_4));  // open: carry, clr

  // Other names for the same wires on the sheet: CLK = in_4; IN[7:0] = in_1
endmodule

module RAM (
  input  [7:0] in_1,
  input  in_2,
  input  in_3,
  input  in_4,
  input  in_5,
  input  [7:0] in_6,
  input  [15:0] in_7,
  input  in_8,
  input  in_9,
  input  in_10,
  output [7:0] out_11
);

  wire and_1_out, and_2_out, multiplexer_3_out, not_1_out;
  wire [7:0] multiplexer_2_out, register_1_q, register_2_q;
  wire [15:0] multiplexer_1_out;

  not not_1 (not_1_out, in_3);
  and and_1 (and_1_out, in_2, in_3);
  and and_2 (and_2_out, not_1_out, in_2);
  Register register_1 (.D(in_1), .en(and_1_out), .Q(register_1_q), .clk(in_5));  // open: clr
  Register register_2 (.D(in_1), .en(and_2_out), .Q(register_2_q), .clk(in_5));  // open: clr
  Multiplexer #(.width(16), .enable("false")) multiplexer_1 (
    .in0({register_2_q, register_1_q}), .in1(in_7), .out(multiplexer_1_out), .sel(in_10));
  Multiplexer #(.width(8), .enable("false")) multiplexer_2 (
    .in0(in_1), .in1(in_6), .out(multiplexer_2_out), .sel(in_10));
  Multiplexer #(.enable("false")) multiplexer_3 (.in0(in_8), .in1(in_9), .out(multiplexer_3_out), .sel(in_10));
  RAM_part #(.addrWidth(16), .bus("separate")) ram_1 (
    .addr(multiplexer_1_out), .din(multiplexer_2_out), .data(out_11), .str(multiplexer_3_out), .clk(in_5),
    .ld(in_4));  // open: sel, clr

  // Other names for the same wires on the sheet: CLK = in_5; IN[7:0] = in_1
endmodule

module INST_REG (
  input  [7:0] in_1,
  input  in_2,
  input  in_3,
  output [7:0] out_4
);

  Register register_1 (.D(in_1), .en(in_2), .Q(out_4), .clk(in_3));  // open: clr
endmodule

module CONTROL (
  input  [7:0] in_1,
  input  in_2,
  input  in_3,
  input  in_4,
  output out_5,
  output out_6,
  output out_7,
  output out_8,
  output out_9,
  output out_10,
  output out_11,
  output out_12,
  output out_13,
  output out_14,
  output out_15,
  output out_16,
  output out_17,
  output out_18
);

  wire counter_1_carry, not_1_out;
  wire [1:0] undriven;
  wire [3:3] counter_1_q_2;
  wire [12:10] counter_1_q;

  Counter #(.width(4), .max('hf)) counter_1 (
    .count(not_1_out), .Q({counter_1_q_2[3], counter_1_q}), .carry(counter_1_carry), .clk(not_1_out));  // open: load, D, clr
  not not_1 (not_1_out, in_4);
  Decoder #(.select(3), .enable("false")) decoder_1 (
    .out3(counter_1_carry), .sel({counter_1_q[12], undriven}));  // open: out0, out1, out2, out4, out5, out6, out7
  ROM #(.addrWidth(13), .dataWidth(14)) rom_1 (
    .addr({counter_1_q, in_3, in_2, in_1}),
    .data({out_18, out_17, out_16, out_15, out_14, out_13, out_12, out_11, out_10, out_9, out_8, out_7, out_6, out_5}));  // open: sel

  // Notes on the sheet:
  //   2x  28c16
  //   contents of rom_1 (hex, n*v repeats v):
  //   16*0 1 1006*0 1111
endmodule

module CPU (
  input  in_1,
  input  [15:0] in_2,
  input  [7:0] in_3,
  input  in_4
);

  wire AI, AL, ALUSUB, ALUW, BI, button_1_out, button_2_out, CF, CLK, HLT, INSTEN, PCLE, PCLRS, PCOUNT,
       RAMBLOAD, RAMLRS, RAMWD, SLC_ADDR, ZF;
  wire [7:0] _8BUS, a_reg_1_out_5, b_reg_1_out_4, inst_reg_1_out_4;
  wire [15:0] _16BUS;

  Button button_1 (.out(button_1_out));
  Button button_2 (.out(button_2_out));
  CLK clk_1 (.HLT(HLT), .CLK(CLK), .A_M(button_1_out), .MCLK(button_2_out));
  PC pc_1 (.in_1(_8BUS), .in_2(PCLE), .in_3(PCLRS), .in_5(PCOUNT), .in_4(CLK), .out_6(_16BUS));
  RAM ram_1 (
    .in_1(_8BUS), .in_3(RAMLRS), .in_5(CLK), .out_11(_8BUS), .in_10(in_1), .in_8(RAMWD), .in_4(RAMBLOAD),
    .in_7(in_2), .in_2(SLC_ADDR), .in_6(in_3), .in_9(in_4));
  INST_REG inst_reg_1 (.in_1(_8BUS), .in_2(INSTEN), .in_3(CLK), .out_4(inst_reg_1_out_4));
  A_Reg a_reg_1 (.in_1(CLK), .in_2(_8BUS), .in_3(AI), .out_5(a_reg_1_out_5), .out_6(_8BUS), .in_4(AL));
  B_REG b_reg_1 (.in_1(_8BUS), .in_2(BI), .in_3(CLK), .out_4(b_reg_1_out_4));
  CONTROL control_1 (
    .in_1(inst_reg_1_out_4), .in_2(CF), .in_3(ZF), .out_5(HLT), .out_6(AI), .out_7(AL), .out_8(BI),
    .out_9(ALUW), .out_10(ALUSUB), .out_11(PCLE), .out_12(PCLRS), .out_13(RAMLRS), .out_14(SLC_ADDR),
    .out_15(RAMWD), .out_16(RAMBLOAD), .out_17(INSTEN), .out_18(PCOUNT), .in_4(CLK));
  ALU alu_1 (
    .in_1(a_reg_1_out_5), .in_2(b_reg_1_out_4), .in_3(ALUW), .in_4(ALUSUB), .out_5(_8BUS), .out_7(ZF),
    .out_6(CF));
endmodule
